# Fritzing sketch diagram (saved by Fritzing 0.9.2b)

parts:
  Teensy_3_1 = Teensy 3.1
  SparkFun_9DoF_Sensor_Stick1 = SparkFun 9DoF Sensor Stick [part_number=SEN-13944]

nets:
  GND: Teensy_3_1.GND, SparkFun_9DoF_Sensor_Stick1.GND
  N1: Teensy_3_1.A4/D18, SparkFun_9DoF_Sensor_Stick1.SDA
  N2: Teensy_3_1.A5/D19, SparkFun_9DoF_Sensor_Stick1.SCL
  3V3: Teensy_3_1.3V3, SparkFun_9DoF_Sensor_Stick1.VDD

custom parts:
  SparkFun 9DoF Sensor Stick: Description: The SparkFun 9DoF Sensor Stick is an easy-to-use 9 Degrees of Freedom IMU. The Sensor Stick deftly utilizes the LSM9DS1 motion-sensing system-in-a-chip, the same IC used in the SparkFun 9DoF IMU Breakout. It houses a 3-axis accelerometer, 3-axis gyroscope, and 3-axis magnetometer – nine degrees of freedom (9DoF) in a single IC! The onboard LSM9DS1 is equipped with a digital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
